# Fritzing sketch MBusino_V03 (saved by Fritzing 1.0.0rc)
circuit board: 9.3cm x 6cm
breadboards: 2

parts:
  WeMos_D1_Mini1 = WeMos D1 Mini
  R1 = Resistor [tolerance=±5% power=0.25W resistance=4.7k package=THT]
  R2 = Resistor [tolerance=±5% power=0.25W resistance=4.7k package=THT]
  R3 = Resistor [tolerance=±5% power=0.25W resistance=4.7k package=THT]
  R4 = Resistor [tolerance=±5% power=0.25W resistance=4.7k package=THT]
  R5 = Resistor [tolerance=±5% power=0.25W resistance=4.7k package=THT]
  MBUS1 = female pin header, 6 pins [form="♀ (female)"]
  MBUS2 = female pin header, 6 pins [form="♀ (female)"]
  +_MBUS_- = Camdenboss CTB0158-2 [part_number=CTB0158-2 package=THT]
  S2 = screw terminal, 3 pins [part_number="3V3  GND  DAT"]
  S3 = screw terminal, 3 pins
  S4 = screw terminal, 3 pins
  S5 = screw terminal, 3 pins [part_number="3V3  GND  DAT"]
  I²C = screw terminal, 4 pins [part_number="Gnd 3V3 SCL SDA"]
  S1 = screw terminal, 3 pins

nets:
  N1: WeMos_D1_Mini1.3V3, R1.Pin_1, R2.Pin_1, R3.Pin_1, R4.Pin_1, R5.Pin_1, MBUS1.pin1, S2.pin3, S3.pin3, S4.pin3, S5.pin3, I²C.pin2, S1.pin3
  N2: WeMos_D1_Mini1.5V, MBUS1.pin6
  N3: WeMos_D1_Mini1.D1, I²C.pin3
  N4: WeMos_D1_Mini1.D2, I²C.pin4
  N5: WeMos_D1_Mini1.D3, R5.Pin_0, S5.pin1
  N6: WeMos_D1_Mini1.D4, R1.Pin_0, S1.pin1
  N7: WeMos_D1_Mini1.D5, R4.Pin_0, S4.pin1
  N8: WeMos_D1_Mini1.D6, R3.Pin_0, S3.pin1
  N9: WeMos_D1_Mini1.D7, R2.Pin_0, S2.pin1
  N10: WeMos_D1_Mini1.G, MBUS1.pin5, S2.pin2, S3.pin2, S4.pin2, S5.pin2, I²C.pin1, S1.pin2
  N11: WeMos_D1_Mini1.RX, MBUS1.pin4
  N12: WeMos_D1_Mini1.TX, MBUS1.pin3
  N13: MBUS2.pin1, MBUS2.pin2, MBUS2.pin3, +_MBUS_-.pin2
  N14: MBUS2.pin4, MBUS2.pin5, MBUS2.pin6, +_MBUS_-.pin1

notes:
  GND 3V3 SCL SDA
  DAT GND 3V3
  3V3 TTL VCC
  5V VIN
  Overload NC
  TX
  RX
  GND
