# Fritzing sketch MBusino_V05 (saved by Fritzing 1.0.0rc)
circuit board: 9.3cm x 6cm
breadboards: 2

parts:
  R1 = Resistor [tolerance=±5% power=0.25W resistance=4.7k package=THT]
  R2 = Resistor [tolerance=±5% power=0.25W resistance=4.7k package=THT]
  R3 = Resistor [tolerance=±5% power=0.25W resistance=4.7k package=THT]
  R4 = Resistor [tolerance=±5% power=0.25W resistance=4.7k package=THT]
  R5 = Resistor [tolerance=±5% power=0.25W resistance=4.7k package=THT]
  MBUS1 = female pin header, 6 pins [form="♀ (female)"]
  MBUS2 = female pin header, 6 pins [form="♀ (female)"]
  S2 = screw terminal, 3 pins [part_number="3V3  GND  DAT"]
  S3 = screw terminal, 3 pins
  S4 = screw terminal, 3 pins
  S5 = screw terminal, 3 pins [part_number="3V3  GND  DAT"]
  I²C = screw terminal, 4 pins [part_number="Gnd 3V3 SCL SDA"]
  S1 = screw terminal, 3 pins
  +MBUS-_GND<->V = Camdenboss CTB0158-4 [part_number=CTB0158-4 package=THT]
  R6 = Resistor [tolerance=±5% power=0.25W resistance=4.7k package=THT]
  R7 = Resistor [tolerance=±5% power=0.25W resistance=4.7k package=THT]
  R8 = Resistor [tolerance=±5% power=0.25W resistance=220 package=THT]
  WeMos_D1_Mini1 = WeMos D1 Mini

nets:
  N1: R1.Pin_0, S1.pin2, WeMos_D1_Mini1.D4
  N2: R1.Pin_1, R2.Pin_1, R3.Pin_1, R4.Pin_1, R5.Pin_1, MBUS1.pin1, S2.pin3, S3.pin3, S4.pin3, S5.pin3, I²C.pin4, S1.pin3, R6.Pin_0, R7.Pin_1, R8.Pin_1, WeMos_D1_Mini1.3V3
  N3: R2.Pin_0, S2.pin2, WeMos_D1_Mini1.D7
  N4: R3.Pin_0, S3.pin2, WeMos_D1_Mini1.D6
  N5: R4.Pin_0, S4.pin2, WeMos_D1_Mini1.D5
  N6: R5.Pin_0, S5.pin2, WeMos_D1_Mini1.D3
  N7: MBUS1.pin3, WeMos_D1_Mini1.TX
  N8: MBUS1.pin4, WeMos_D1_Mini1.RX
  N9: MBUS1.pin5, S2.pin1, S3.pin1, S4.pin1, S5.pin1, I²C.pin2, S1.pin1, +MBUS-_GND<->V.pin2, WeMos_D1_Mini1.G
  N10: MBUS1.pin6, WeMos_D1_Mini1.5V
  N11: MBUS2.pin1, MBUS2.pin2, MBUS2.pin3, +MBUS-_GND<->V.pin3
  N12: MBUS2.pin4, MBUS2.pin5, MBUS2.pin6, +MBUS-_GND<->V.pin4
  N13: I²C.pin1, R6.Pin_1, WeMos_D1_Mini1.D2
  N14: I²C.pin3, R7.Pin_0, WeMos_D1_Mini1.D1
  N15: +MBUS-_GND<->V.pin1, R8.Pin_0

notes:
  3V3 SCL GND SDA
  3V3 DAT GND
  3V3 TTL VCC
  5V VIN
  Overload NC
  TX
  RX
  GND
  (DAT6    DAT7)
  V0.5
  R6,R7 (4.7K)
  for S6,S7
  optional
  3V3
  V
